# Fritzing sketch Schema (saved by Fritzing 0.9.1b)
circuit board: 8.46667cm x 5.64444cm
breadboards: 1

parts:
  Componente1 = Arduino Nano (Rev3.0)
  U1 = ESP8266 WiFi Module [part_number=ESP8266]
  S1 = Momentary Switch [package=ksa_sealed_tac_switch]
  R2 = Resistor [tolerance=±5% resistance=220 package=THT]
  R1 = Resistor [tolerance=±5% resistance=10k package=THT]
  LED1 = LED - 3mm [color="Blue (470nm)" package="3 mm [THT]"]

nets:
  GND: Componente1.GND, U1.GND, R1.Pin_0, LED1.cathode
  N1: Componente1.D12/MISO, U1.GPIO_16
  N2: Componente1.A5, U1.RXD
  N3: Componente1.A4, U1.TXD
  3V3: Componente1.3V3, U1.VCC, U1.CH_PD, S1.1, S1.2
  N4: U1.GPIO_0, R2.Pin_1
  N5: U1.GPIO_2, S1.3, S1.4, R1.Pin_1
  N6: R2.Pin_0, LED1.anode

custom parts:
  ESP8266 WiFi Module: Generic WiFi Module based on the ESP8266 with onboard PCB antenna and UART communications
